# Fritzing sketch shift-register (saved by Fritzing 0.9.3b)
breadboards: 2

parts:
  Part1 = Arduino Uno (Rev3) - ICSP
  U1 = 74HC595 SMD [package="SO16 [SMD]"]
  U2 = Voltage Regulator - 5V [package="TO220 [THT]"]
  U3 = Voltage Regulator - 5V [package="TO220 [THT]"]
  U4 = Voltage Regulator - 5V [package="TO220 [THT]"]
  VCC1 = 4 x AAA Battery Mount
  M1 = DC Motor
  M2 = DC Motor
  M3 = DC Motor

nets:
  N1: Part1.ICSP_MOSI, Part1.D11_PWM/MOSI, U1.DS
  N2: Part1.D8, U1.ST_CP
  N3: Part1.D12/MISO, U1.SH_CP
  N4: Part1.GND, U1.OE
  5V: Part1.5V, U1.MR, U1.VCC
  N5: U1.Q1, U3.input_voltage
  N6: U1.Q2, U4.input_voltage
  N7: U1.Q0, U2.input_voltage
  N8: U2.GND, M3.pin_1
  N9: U2.output_voltage, U3.output_voltage, U4.output_voltage, VCC1.-
  N10: U3.GND, M2.pin_1
  N11: U4.GND, M1.pin_1
  N12: VCC1.+, M1.pin_2, M2.pin_2, M3.pin_2
