# Fritzing sketch attiny-i2c-example (saved by Fritzing 0.9.3b)
breadboards: 1

parts:
  U1 = attiny85 [package=dip]
  Part1 = Arduino Uno (Rev3)
  LED1 = LED - 3mm [color="Red (633nm)" package="3 mm [THT]"]

nets:
  N1: U1.Pin_4, Part1.GND, LED1.cathode
  N2: U1.Pin_5, Part1.A4/SDA
  N3: U1.Pin_6, LED1.anode
  N4: U1.Pin_7, Part1.A5/SCL
  N5: U1.Pin_8, Part1.5V
