# Fritzing sketch bluetooth-led (saved by Fritzing 0.9.3b)
breadboards: 1

parts:
  Part1 = Arduino Uno (Rev3)
  Part2 = Bluetooth Mate Silver
  LED1 = smd LED [color="Red (633nm)" package="0603 [SMD]"]

nets:
  N1: Part1.D13/SCK, LED1.anode
  N2: Part1.D2, Part2.VCC
  N3: Part1.D3_PWM, Part2.CTS_5V
  N4: Part1.5V, Part2.RX_5V
  N5: Part1.GND, Part2.TX_5V, LED1.cathode
