# Fritzing sketch esp8266-motor-control (saved by Fritzing 0.9.3b)
breadboards: 1

parts:
  Part1 = SparkFun ESP8266 Thing
  Part2 = Motor Driver 1A Dual TB6612FNG
  M1 = DC Motor
  M2 = DC Motor
  VCC1 = Battery
  LED1 = LED - 3mm [color="Red (633nm)" package="3 mm [THT]"]

nets:
  GND: Part1.GND, Part2.GND, VCC1.-, LED1.cathode
  N1: Part1.GPIO2, LED1.anode
  N2: Part1.USBVCC, Part2.VCC
  N3: Part1.GPIO5, Part2.PWMA
  N4: Part1.GPIO0, Part2.AIN2
  N5: Part1.GPIO4, Part2.AIN1
  N6: Part1.GPIO13, Part2.STBY
  N7: Part1.GPIO12, Part2.BIN1
  N8: Part1.GPIO16, Part2.BIN2
  N9: Part1.GPIO15, Part2.PWMB
  N10: Part2.B01, M2.pin_1
  N11: Part2.B02, M2.pin_2
  N12: Part2.A02, M1.pin_1
  N13: Part2.A01, M1.pin_2
  N14: Part2.VM, VCC1.+
