# Fritzing sketch esp8266-web-shift-register (saved by Fritzing 0.9.3b)
breadboards: 1

parts:
  Part1 = SparkFun ESP8266 Thing
  U1 = 74HC595 [package="DIP16 [THT]"]
  LED1 = smd LED [color="Red (633nm)" package="0805 [SMD]"]
  LED2 = smd LED [color="Red (633nm)" package="0805 [SMD]"]
  LED3 = smd LED [color="Red (633nm)" package="0805 [SMD]"]
  LED4 = smd LED [color="Red (633nm)" package="0805 [SMD]"]

nets:
  N1: Part1.USBVCC, U1.MR, U1.VCC
  N2: Part1.GND, U1.OE
  N3: Part1.GPIO13, U1.SH_CP
  N4: Part1.GPIO12, U1.ST_CP
  N5: Part1.GPIO16, U1.DS
  N6: U1.Q1, LED2.anode
  N7: U1.Q2, LED3.anode
  N8: U1.Q3, LED4.anode
  N9: U1.Q0, LED1.anode
  N10: LED1.cathode, LED2.cathode, LED3.cathode, LED4.cathode
