# Fritzing sketch motor-control (saved by Fritzing 0.9.3b)
breadboards: 1

parts:
  Part1 = Arduino Uno (Rev3)
  Part2 = Motor Driver 1A Dual TB6612FNG
  M1 = DC Motor
  M2 = DC Motor

nets:
  N1: Part1.D8, Part2.BIN2
  N2: Part1.D9_PWM, Part2.PWMB
  N3: Part1.D3_PWM, Part2.PWMA
  N4: Part1.D4, Part2.AIN2
  N5: Part1.D5_PWM, Part2.AIN1
  N6: Part1.D6_PWM, Part2.STBY
  N7: Part1.D7, Part2.BIN1
  5V: Part1.5V, Part2.VCC
  N8: Part2.B01, M1.pin_1
  N9: Part2.B02, M1.pin_2
  N10: Part2.A02, M2.pin_1
  N11: Part2.A01, M2.pin_2
