# Fritzing sketch prototype (saved by Fritzing 0.9.3b)
breadboards: 1

parts:
  IC1 = SHIFT REGISTER [package=dil16]
  Q1 = Basic FET P-Channel [package="D2Pak [SMD]"]
  M1 = DC Motor
  VCC1 = Battery
  Q2 = Basic FET P-Channel [package="D2Pak [SMD]"]

nets:
  N1: IC1.QC, IC1.GND
  N2: IC1.QF, VCC1.-, Q2.source
  N3: IC1.QH, Q1.Gate
  N4: IC1.QH*, Q2.Gate
  N5: Q1.drain, VCC1.+
  N6: Q1.source, M1.pin_2
  N7: M1.pin_1, Q2.drain
